// Logisim project LC-2200-16.circ as structural Verilog: 3 circuits, main circuit main
module main (
  output [15:0] out_1,
  output [3:0] out_2,
  output [1:0] out_3
);

  wire ALUHi, ALULo, chkZ, Clock, comparator_1_eq, DrALU, DrMEM, DrOFF, DrPC, DrREG, LdA, LdB, LdIR, LdMAR,
       LdPC, LdZ, OPTest, WrMEM, WrREG, Z;
  wire [0:0] IR_q;
  wire [2:0] OP;
  wire [3:0] RX, RY, RZ;
  wire [4:0] bitselector_1_out;
  wire [5:0] multiplexer_1_out, Next_State, rom_1_data, rom_2_data, State_Register_q;
  wire [15:0] A, alu_1_out_4, B, bit_extender_1_out, MAR_q, PC_q, Register_File_output;

  Clock clock_1 (.out(Clock));
  Register #(.width(16)) PC (.D(out_1), .en(LdPC), .Q(PC_q), .clk(Clock));  // open: clr
  assign out_1 = DrPC ? PC_q : 16'bz;  // Controlled_Buffer controlled_buffer_1
  Register #(.width(6)) State_Register (.D(multiplexer_1_out), .Q(State_Register_q), .clk(Clock));  // open: en, clr
  Multiplexer #(.select(2), .width(6)) multiplexer_1 (
    .in0(Next_State), .in1(rom_2_data), .in2(rom_1_data), .out(multiplexer_1_out), .sel({chkZ, OPTest}));  // open: in3, en
  Register #(.width(16)) u_A (.D(out_1), .en(LdA), .Q(A), .clk(Clock));  // open: clr
  ALU alu_1 (.A(A), .B(B), .FUNC({ALUHi, ALULo}), .out_4(alu_1_out_4));
  assign out_1 = DrALU ? alu_1_out_4 : 16'bz;  // Controlled_Buffer controlled_buffer_2
  ROM #(.addrWidth(2), .dataWidth(6)) rom_1 (.addr({1'b0, Z}), .data(rom_1_data));  // open: sel
  ROM #(.addrWidth(3), .dataWidth(6)) rom_2 (.addr(OP), .data(rom_2_data));  // open: sel
  Register #(.width(16)) u_B (.D(out_1), .en(LdB), .Q(B), .clk(Clock));  // open: clr
  Register_FIle Register_File (
    .Input(out_1), .WrREG(WrREG), .regno(out_2), .Clock(Clock), .Output(Register_File_output));
  assign out_1 = DrREG ? Register_File_output : 16'bz;  // Controlled_Buffer controlled_buffer_3
  ROM #(.addrWidth(6), .dataWidth(25)) rom_3 (
    .addr(State_Register_q),
    .data({chkZ, OPTest, ALUHi, ALULo, out_3, WrMEM, WrREG, LdZ, LdB, LdA, LdMAR, LdIR, LdPC, DrOFF, DrPC, DrALU, DrMEM, DrREG, Next_State}));  // open: sel
  Register #(.width(16)) MAR (.D(out_1), .en(LdMAR), .Q(MAR_q), .clk(Clock));  // open: clr
  RAM #(.addrWidth(16), .dataWidth(16), .bus("separate")) ram_1 (
    .addr(MAR_q), .din(out_1), .data(out_1), .str(WrMEM), .clk(Clock), .ld(DrMEM));  // open: sel, clr
  Comparator #(.width(16)) comparator_1 (.a(out_1), .b({16{1'b0}}), .eq(comparator_1_eq));  // open: gt, lt
  Register #(.width(16)) IR (.D(out_1), .en(LdIR), .Q({OP, RX, RY, RZ, IR_q[0]}), .clk(Clock));  // open: clr
  BitSelector #(.width(16), .group(5)) bitselector_1 (
    .in({OP, RX, RY, RZ, IR_q[0]}), .out(bitselector_1_out), .sel(2'b00));
  assign bit_extender_1_out = {{11{bitselector_1_out[4]}}, bitselector_1_out};  // Bit_Extender bit_extender_1
  assign out_1 = DrOFF ? bit_extender_1_out : 16'bz;  // Controlled_Buffer controlled_buffer_4
  Register #(.width(1)) register_1 (.D(comparator_1_eq), .en(LdZ), .Q(Z), .clk(Clock));  // open: clr
  Multiplexer #(.select(2), .width(4)) multiplexer_2 (
    .in0(RX), .in1(RY), .in2(RZ), .out(out_2), .sel(out_3));  // open: in3, en

  // Other names for the same wires on the sheet: RegSelLo = out_3[0]; RegSelHi = out_3[1]; regno[3:0] = out_2

  // Notes on the sheet:
  //   SPRING 2016
  //   contents of rom_1 (hex, n*v repeats v):
  //   0 1b
  //   contents of rom_2 (hex, n*v repeats v):
  //   3 6 c f 13 17 1e 20
  //   contents of rom_3 (hex, n*v repeats v):
  //   6201 1082 e00900 84044 108045 20100 8c047 404108 420100 10404a 8804b 220100 8404d 840e 20100 84050
  //   8411 2112 20080 84054 8415 2116 40040 4058 88059 41011a 1000000 421c 841d 900 a021f 840 20
endmodule

module Register_FIle (
  input  [15:0] Input,
  input  WrREG,
  input  [3:0] regno,
  input  Clock,
  output [15:0] Output
);

  wire _0, _1, _2, _3, _4, _5, _6, _7, _8, _9, _10, _11, _12, _13, _14, _15;
  wire [15:0] Out0, Out1, Out2, Out3, Out4, Out5, Out6, Out7, Out8, Out9, Out10, Out11, Out12, Out13, Out14,
       Out15;

  Decoder #(.select(4), .disabled(0)) decoder_1 (
    .out0(_0), .out1(_1), .out2(_2), .out3(_3), .out4(_4), .out5(_5), .out6(_6), .out7(_7), .out8(_8),
    .out9(_9), .out10(_10), .out11(_11), .out12(_12), .out13(_13), .out14(_14), .out15(_15), .sel(regno),
    .en(WrREG));
  Register #(.width(16)) Zero (.D(Input), .en(1'b0), .Q(Out0), .clk(Clock));  // open: clr
  Register #(.width(16)) at (.D(Input), .en(_1), .Q(Out1), .clk(Clock));  // open: clr
  Register #(.width(16)) v0 (.D(Input), .en(_2), .Q(Out2), .clk(Clock));  // open: clr
  Register #(.width(16)) a0 (.D(Input), .en(_3), .Q(Out3), .clk(Clock));  // open: clr
  Register #(.width(16)) a1 (.D(Input), .en(_4), .Q(Out4), .clk(Clock));  // open: clr
  Register #(.width(16)) a2 (.D(Input), .en(_5), .Q(Out5), .clk(Clock));  // open: clr
  Register #(.width(16)) t0 (.D(Input), .en(_6), .Q(Out6), .clk(Clock));  // open: clr
  Register #(.width(16)) t1 (.D(Input), .en(_7), .Q(Out7), .clk(Clock));  // open: clr
  Register #(.width(16)) t2 (.D(Input), .en(_8), .Q(Out8), .clk(Clock));  // open: clr
  Register #(.width(16)) s0 (.D(Input), .en(_9), .Q(Out9), .clk(Clock));  // open: clr
  Register #(.width(16)) s1 (.D(Input), .en(_10), .Q(Out10), .clk(Clock));  // open: clr
  Register #(.width(16)) s2 (.D(Input), .en(_11), .Q(Out11), .clk(Clock));  // open: clr
  Register #(.width(16)) k0 (.D(Input), .en(_12), .Q(Out12), .clk(Clock));  // open: clr
  Register #(.width(16)) sp (.D(Input), .en(_13), .Q(Out13), .clk(Clock));  // open: clr
  Register #(.width(16)) fp (.D(Input), .en(_14), .Q(Out14), .clk(Clock));  // open: clr
  Register #(.width(16)) ra (.D(Input), .en(_15), .Q(Out15), .clk(Clock));  // open: clr
  Multiplexer #(.select(4), .width(16)) multiplexer_1 (
    .in0(Out0), .in1(Out1), .in2(Out2), .in3(Out3), .in4(Out4), .in5(Out5), .in6(Out6), .in7(Out7),
    .in8(Out8), .in9(Out9), .in10(Out10), .in11(Out11), .in12(Out12), .in13(Out13), .in14(Out14),
    .in15(Out15), .out(Output), .sel(regno));  // open: en
endmodule

module ALU (
  input  [15:0] A,
  input  [15:0] B,
  input  [1:0] FUNC,
  output [15:0] out_4
);

  wire [15:0] ADD, INC, NAND, NAND_out, SUBT;

  Adder #(.width(16)) adder_1 (.a(A), .b(B), .out(ADD));  // open: cin, cout
  assign NAND_out = A & B;  // AND_Gate NAND, 16 bits wide
  assign NAND = ~NAND_out;  // NOT_Gate not_1, 16 bits wide
  Subtractor #(.width(16)) subtractor_1 (.a(A), .b(B), .out(SUBT));  // open: bin, bout
  Adder #(.width(16)) adder_2 (.a(A), .b(16'h1), .out(INC));  // open: cin, cout
  Multiplexer #(.select(2), .width(16), .enable("false")) multiplexer_1 (
    .in0(ADD), .in1(NAND), .in2(SUBT), .in3(INC), .out(out_4), .sel(FUNC));
endmodule
